// Logisim project temp.circ as structural Verilog: 1 circuit, main circuit main
module main (
  input  in_1,
  input  in_2,
  input  in_3,
  input  in_4,
  input  in_5,
  input  in_6,
  output out_7
);

  wire and_1_out, and_2_out, d_ff_1_q, d_ff_2_q, multiplexer_1_out, not_1_out, not_2_out, not_3_out;

  not not_1 (not_1_out, d_ff_1_q);
  D_Flip_Flop d_ff_1 (.D(not_1_out), .clk(in_1), .Q(d_ff_1_q));  // open: Qn, preset, reset
  D_Flip_Flop d_ff_2 (.D(multiplexer_1_out), .clk(in_2), .Q(d_ff_2_q));  // open: Qn, preset, reset
  not not_2 (not_2_out, in_6);
  not not_3 (not_3_out, d_ff_2_q);
  and and_1 (and_1_out, in_4, in_6);
  and and_2 (and_2_out, in_5, not_2_out);
  Multiplexer multiplexer_1 (.in0(d_ff_2_q), .in1(not_3_out), .out(multiplexer_1_out), .sel(in_3));
  or or_1 (out_7, and_1_out, and_2_out);
endmodule
